// Logisim project wire.circ as structural Verilog: 8 circuits, main circuit main
module main (
);

  wire button_1_out, button_2_out, button_3_out, step1_1_is_start;
  wire [3:0] step1_1_minutes_1, step1_1_minutes_2, step1_1_seconds_1, step1_1_seconds_2,
       step1_1_split_1_min_1, step1_1_split_1_min_2, step1_1_split_1_sec_1, step1_1_split_1_sec_2,
       step1_1_split_2_min_1, step1_1_split_2_min_2, step1_1_split_2_sec_1, step1_1_split_2_sec_2,
       step1_1_split_3_min_1, step1_1_split_3_min_2, step1_1_split_3_sec_1, step1_1_split_3_sec_2,
       step1_1_split_4_min_1, step1_1_split_4_min_2, step1_1_split_4_sec_1, step1_1_split_4_sec_2,
       step1_1_split_5_min_1, step1_1_split_5_min_2, step1_1_split_5_sec_1, step1_1_split_5_sec_2,
       step1_1_split_min_1, step1_1_split_min_2, step1_1_split_sec_1, step1_1_split_sec_2;

  Hex_Digit_Display hex_digit_display_1 (.value(step1_1_minutes_1));  // open: dp
  Hex_Digit_Display hex_digit_display_2 (.value(step1_1_minutes_2));  // open: dp
  Step1 step1_1 (
    .START(button_1_out), .SPLIT(button_2_out), .RESET(button_3_out), .is_Start(step1_1_is_start),
    .Split_1_Min_1(step1_1_split_1_min_1), .Split_1_Min_2(step1_1_split_1_min_2),
    .Split_1_Sec_1(step1_1_split_1_sec_1), .Split_1_Sec_2(step1_1_split_1_sec_2),
    .Split_2_Min_1(step1_1_split_2_min_1), .Split_2_Min_2(step1_1_split_2_min_2),
    .Split_2_Sec_1(step1_1_split_2_sec_1), .Split_2_Sec_2(step1_1_split_2_sec_2),
    .Split_3_Min_1(step1_1_split_3_min_1), .Split_3_Min_2(step1_1_split_3_min_2),
    .Split_3_Sec_1(step1_1_split_3_sec_1), .Split_3_Sec_2(step1_1_split_3_sec_2),
    .Split_4_Min_1(step1_1_split_4_min_1), .Split_4_Min_2(step1_1_split_4_min_2),
    .Split_4_Sec_1(step1_1_split_4_sec_1), .Split_4_Sec_2(step1_1_split_4_sec_2),
    .Split_5_Min_1(step1_1_split_5_min_1), .Split_5_Min_2(step1_1_split_5_min_2),
    .Split_5_Sec_1(step1_1_split_5_sec_1), .Split_5_Sec_2(step1_1_split_5_sec_2),
    .Split_Min_1(step1_1_split_min_1), .Split_Min_2(step1_1_split_min_2), .Split_Sec_1(step1_1_split_sec_1),
    .Split_Sec_2(step1_1_split_sec_2), .Minutes_1(step1_1_minutes_1), .Minutes_2(step1_1_minutes_2),
    .Seconds_1(step1_1_seconds_1), .Seconds_2(step1_1_seconds_2));
  Button button_1 (.out(button_1_out));
  Hex_Digit_Display hex_digit_display_3 (.value(step1_1_seconds_1));  // open: dp
  Button button_2 (.out(button_2_out));
  Hex_Digit_Display hex_digit_display_4 (.value(step1_1_seconds_2));  // open: dp
  Button button_3 (.out(button_3_out));
  Hex_Digit_Display hex_digit_display_5 (.value(step1_1_split_min_1));  // open: dp
  Hex_Digit_Display hex_digit_display_6 (.value(step1_1_split_min_2));  // open: dp
  Hex_Digit_Display hex_digit_display_7 (.value(step1_1_split_sec_1));  // open: dp
  LED led_1 (.in(step1_1_is_start));
  Hex_Digit_Display hex_digit_display_8 (.value(step1_1_split_sec_2));  // open: dp
  Hex_Digit_Display hex_digit_display_9 (.value(step1_1_split_1_min_1));  // open: dp
  Hex_Digit_Display hex_digit_display_10 (.value(step1_1_split_1_min_2));  // open: dp
  Hex_Digit_Display hex_digit_display_11 (.value(step1_1_split_1_sec_1));  // open: dp
  Hex_Digit_Display hex_digit_display_12 (.value(step1_1_split_1_sec_2));  // open: dp
  Hex_Digit_Display hex_digit_display_13 (.value(step1_1_split_2_min_1));  // open: dp
  Hex_Digit_Display hex_digit_display_14 (.value(step1_1_split_2_min_2));  // open: dp
  Hex_Digit_Display hex_digit_display_15 (.value(step1_1_split_2_sec_1));  // open: dp
  Hex_Digit_Display hex_digit_display_16 (.value(step1_1_split_2_sec_2));  // open: dp
  Hex_Digit_Display hex_digit_display_17 (.value(step1_1_split_3_min_1));  // open: dp
  Hex_Digit_Display hex_digit_display_18 (.value(step1_1_split_3_min_2));  // open: dp
  Hex_Digit_Display hex_digit_display_19 (.value(step1_1_split_3_sec_1));  // open: dp
  Hex_Digit_Display hex_digit_display_20 (.value(step1_1_split_3_sec_2));  // open: dp
  Hex_Digit_Display hex_digit_display_21 (.value(step1_1_split_4_min_1));  // open: dp
  Hex_Digit_Display hex_digit_display_22 (.value(step1_1_split_4_min_2));  // open: dp
  Hex_Digit_Display hex_digit_display_23 (.value(step1_1_split_4_sec_1));  // open: dp
  Hex_Digit_Display hex_digit_display_24 (.value(step1_1_split_4_sec_2));  // open: dp
  Hex_Digit_Display hex_digit_display_25 (.value(step1_1_split_5_min_1));  // open: dp
  Hex_Digit_Display hex_digit_display_26 (.value(step1_1_split_5_min_2));  // open: dp
  Hex_Digit_Display hex_digit_display_27 (.value(step1_1_split_5_sec_1));  // open: dp
  Hex_Digit_Display hex_digit_display_28 (.value(step1_1_split_5_sec_2));  // open: dp

  // Notes on the sheet:
  //   Minutes
  //   Start
  //   Elapsed Time
  //   :
  //   Stopwatch Interface
  //   Split
  //   Seconds
  //   Reset
  //   Minutes
  //   Clock Started
  //   Split Time
  //   :
  //   Seconds
  //   Minutes
  //   Lap 1
  //   :
  //   Seconds
  //   Minutes
  //   Lap 2
  //   :
  //   Seconds
  //   Minutes
  //   :
  //   Lap 3
  //   Seconds
  //   Minutes
  //   Lap 4
  //   Seconds
  //   :
  //   Minutes
  //   Lap 5
  //   :
  //   Seconds
endmodule

module Step1 (
  input  START,
  input  SPLIT,
  input  RESET,
  output is_Start,
  output [3:0] Split_1_Min_1,
  output [3:0] Split_1_Min_2,
  output [3:0] Split_1_Sec_1,
  output [3:0] Split_1_Sec_2,
  output [3:0] Split_2_Min_1,
  output [3:0] Split_2_Min_2,
  output [3:0] Split_2_Sec_1,
  output [3:0] Split_2_Sec_2,
  output [3:0] Split_3_Min_1,
  output [3:0] Split_3_Min_2,
  output [3:0] Split_3_Sec_1,
  output [3:0] Split_3_Sec_2,
  output [3:0] Split_4_Min_1,
  output [3:0] Split_4_Min_2,
  output [3:0] Split_4_Sec_1,
  output [3:0] Split_4_Sec_2,
  output [3:0] Split_5_Min_1,
  output [3:0] Split_5_Min_2,
  output [3:0] Split_5_Sec_1,
  output [3:0] Split_5_Sec_2,
  output [3:0] Split_Min_1,
  output [3:0] Split_Min_2,
  output [3:0] Split_Sec_1,
  output [3:0] Split_Sec_2,
  output [3:0] Minutes_1,
  output [3:0] Minutes_2,
  output [3:0] Seconds_1,
  output [3:0] Seconds_2
);

  wire and_1_out, d_ff_1_q, or_1_out, step2_1_swtich_second, step3_1_switch_minuet;

  D_Flip_Flop d_ff_1 (.D(is_Start), .clk(or_1_out), .Q(d_ff_1_q));  // open: Qn, preset, reset
  or or_1 (or_1_out, START, and_1_out);
  and and_1 (and_1_out, is_Start, RESET);
  not not_1 (is_Start, d_ff_1_q);
  Step2 step2_1 (.START(is_Start), .RESET(RESET), .SWTICH_SECOND(step2_1_swtich_second), .Right(Seconds_2));
  Step3 step3_1 (
    .SWITCH_SECOND(step2_1_swtich_second), .RESET(RESET), .SWITCH_MINUET(step3_1_switch_minuet),
    .Left(Seconds_1));
  Step4 step4_1 (.SWITCH_MIN(step3_1_switch_minuet), .RESET(RESET), .Left(Minutes_1), .Right(Minutes_2));
  Step5 step5_1 (
    .SPLIT(SPLIT), .is_Start(is_Start), .Reset(RESET), .Minutes_1(Minutes_1), .Minutes_2(Minutes_2),
    .Seconds_1(Seconds_1), .Seconds_2(Seconds_2), .Split_Min_1(Split_Min_1), .Split_Min_2(Split_Min_2),
    .Split_Sec_1(Split_Sec_1), .Split_Sec_2(Split_Sec_2));
  Step6 step6_1 (
    .SPLIT(SPLIT), .is_Start(is_Start), .Reset(RESET), .Split_Min_1(Minutes_1), .Split_Min_2(Minutes_2),
    .Split_Sec_1(Seconds_1), .Split_Sec_2(Seconds_2), .Split_1_Min_1(Split_1_Min_1),
    .Split_1_Min_2(Split_1_Min_2), .Split_1_Sec_1(Split_1_Sec_1), .Split_1_Sec_2(Split_1_Sec_2),
    .Split_2_Min_1(Split_2_Min_1), .Split_2_Min_2(Split_2_Min_2), .Split_2_Sec_1(Split_2_Sec_1),
    .Split_2_Sec_2(Split_2_Sec_2), .Split_3_Min_1(Split_3_Min_1), .Split_3_Min_2(Split_3_Min_2),
    .Split_3_Sec_1(Split_3_Sec_1), .Split_3_Sec_2(Split_3_Sec_2), .Split_4_Min_1(Split_4_Min_1),
    .Split_4_Min_2(Split_4_Min_2), .Split_4_Sec_1(Split_4_Sec_1), .Split_4_Sec_2(Split_4_Sec_2),
    .Split_5_Min_1(Split_5_Min_1), .Split_5_Min_2(Split_5_Min_2), .Split_5_Sec_1(Split_5_Sec_1),
    .Split_5_Sec_2(Split_5_Sec_2));
endmodule

module Step2 (
  input  START,
  input  RESET,
  output SWTICH_SECOND,
  output [3:0] Right
);

  wire clock_1_out, j_k_ff_1_q, j_k_ff_1_qn, j_k_ff_2_q, j_k_ff_2_qn, j_k_ff_3_q, j_k_ff_3_qn, j_k_ff_4_q,
       or_1_out, RESET10_out;

  Clock clock_1 (.out(clock_1_out));
  and RESET10 (RESET10_out, j_k_ff_4_q, j_k_ff_2_q);
  or or_1 (or_1_out, RESET10_out, RESET);
  and RESET9 (SWTICH_SECOND, j_k_ff_4_q, j_k_ff_1_q);
  J_K_Flip_Flop j_k_ff_1 (
    .J(START), .K(START), .clk(clock_1_out), .Q(j_k_ff_1_q), .Qn(j_k_ff_1_qn), .reset(or_1_out));  // open: preset
  D_Flip_Flop #(.trigger("falling")) d_ff_1 (
    .D(j_k_ff_1_q), .clk(clock_1_out), .Q(Right[0]), .reset(or_1_out));  // open: Qn, preset
  J_K_Flip_Flop j_k_ff_2 (
    .J(START), .K(START), .clk(j_k_ff_1_qn), .Q(j_k_ff_2_q), .Qn(j_k_ff_2_qn), .reset(or_1_out));  // open: preset
  D_Flip_Flop #(.trigger("falling")) d_ff_2 (
    .D(j_k_ff_2_q), .clk(clock_1_out), .Q(Right[1]), .reset(or_1_out));  // open: Qn, preset
  J_K_Flip_Flop j_k_ff_3 (
    .J(START), .K(START), .clk(j_k_ff_2_qn), .Q(j_k_ff_3_q), .Qn(j_k_ff_3_qn), .reset(or_1_out));  // open: preset
  J_K_Flip_Flop j_k_ff_4 (
    .J(START), .K(START), .clk(j_k_ff_3_qn), .Q(j_k_ff_4_q), .reset(or_1_out));  // open: Qn, preset
  D_Flip_Flop #(.trigger("falling")) d_ff_3 (
    .D(j_k_ff_3_q), .clk(clock_1_out), .Q(Right[2]), .reset(or_1_out));  // open: Qn, preset
  D_Flip_Flop #(.trigger("falling")) d_ff_4 (
    .D(j_k_ff_4_q), .clk(clock_1_out), .Q(Right[3]), .reset(or_1_out));  // open: Qn, preset
endmodule

module Step3 (
  input  SWITCH_SECOND,
  input  RESET,
  output SWITCH_MINUET,
  output [3:0] Left
);

  wire and_1_out, j_k_ff_1_q, j_k_ff_1_qn, j_k_ff_2_q, j_k_ff_2_qn, j_k_ff_3_q, j_k_ff_3_qn, j_k_ff_4_q,
       RESET6_out;

  J_K_Flip_Flop j_k_ff_1 (
    .J(1'b1), .K(1'b1), .clk(SWITCH_SECOND), .Q(j_k_ff_1_q), .Qn(j_k_ff_1_qn), .reset(RESET6_out));  // open: preset
  J_K_Flip_Flop j_k_ff_2 (
    .J(1'b1), .K(1'b1), .clk(j_k_ff_1_qn), .Q(j_k_ff_2_q), .Qn(j_k_ff_2_qn), .reset(RESET6_out));  // open: preset
  D_Flip_Flop #(.trigger("falling")) d_ff_1 (
    .D(j_k_ff_1_q), .clk(SWITCH_SECOND), .Q(Left[0]), .reset(RESET6_out));  // open: Qn, preset
  D_Flip_Flop #(.trigger("falling")) d_ff_2 (
    .D(j_k_ff_2_q), .clk(SWITCH_SECOND), .Q(Left[1]), .reset(RESET6_out));  // open: Qn, preset
  J_K_Flip_Flop j_k_ff_3 (
    .J(1'b1), .K(1'b1), .clk(j_k_ff_2_qn), .Q(j_k_ff_3_q), .Qn(j_k_ff_3_qn), .reset(RESET6_out));  // open: preset
  D_Flip_Flop #(.trigger("falling")) d_ff_3 (
    .D(j_k_ff_3_q), .clk(SWITCH_SECOND), .Q(Left[2]), .reset(RESET6_out));  // open: Qn, preset
  J_K_Flip_Flop j_k_ff_4 (
    .J(1'b1), .K(1'b1), .clk(j_k_ff_3_qn), .Q(j_k_ff_4_q), .reset(RESET6_out));  // open: Qn, preset
  and and_1 (and_1_out, j_k_ff_2_q, j_k_ff_3_q);
  and and_2 (SWITCH_MINUET, j_k_ff_3_q, j_k_ff_1_q);
  or RESET6 (RESET6_out, RESET, and_1_out);
  D_Flip_Flop #(.trigger("falling")) d_ff_4 (
    .D(j_k_ff_4_q), .clk(SWITCH_SECOND), .Q(Left[3]), .reset(RESET6_out));  // open: Qn, preset
endmodule

module Step4 (
  input  SWITCH_MIN,
  input  RESET,
  output [3:0] Left,
  output [3:0] Right
);

  wire and_1_out, j_k_ff_1_q, j_k_ff_1_qn, j_k_ff_2_q, j_k_ff_2_qn, j_k_ff_3_q, j_k_ff_3_qn, j_k_ff_4_q,
       j_k_ff_5_q, j_k_ff_5_qn, j_k_ff_6_q, j_k_ff_6_qn, j_k_ff_7_q, j_k_ff_7_qn, j_k_ff_8_q, or_1_out,
       RESET9_out, RESET10_2_out, RESET10_out;

  J_K_Flip_Flop j_k_ff_1 (
    .J(1'b1), .K(1'b1), .clk(RESET9_out), .Q(j_k_ff_1_q), .Qn(j_k_ff_1_qn), .reset(RESET10_2_out));  // open: preset
  J_K_Flip_Flop j_k_ff_2 (
    .J(1'b1), .K(1'b1), .clk(j_k_ff_1_qn), .Q(j_k_ff_2_q), .Qn(j_k_ff_2_qn), .reset(RESET10_2_out));  // open: preset
  D_Flip_Flop #(.trigger("falling")) d_ff_1 (
    .D(j_k_ff_1_q), .clk(RESET9_out), .Q(Left[0]), .reset(RESET10_2_out));  // open: Qn, preset
  D_Flip_Flop #(.trigger("falling")) d_ff_2 (
    .D(j_k_ff_2_q), .clk(RESET9_out), .Q(Left[1]), .reset(RESET10_2_out));  // open: Qn, preset
  J_K_Flip_Flop j_k_ff_3 (
    .J(1'b1), .K(1'b1), .clk(j_k_ff_2_qn), .Q(j_k_ff_3_q), .Qn(j_k_ff_3_qn), .reset(RESET10_2_out));  // open: preset
  D_Flip_Flop #(.trigger("falling")) d_ff_3 (
    .D(j_k_ff_3_q), .clk(RESET9_out), .Q(Left[2]), .reset(RESET10_2_out));  // open: Qn, preset
  J_K_Flip_Flop j_k_ff_4 (
    .J(1'b1), .K(1'b1), .clk(j_k_ff_3_qn), .Q(j_k_ff_4_q), .reset(RESET10_2_out));  // open: Qn, preset
  or RESET10_2 (RESET10_2_out, RESET, and_1_out);
  D_Flip_Flop #(.trigger("falling")) d_ff_4 (
    .D(j_k_ff_4_q), .clk(RESET9_out), .Q(Left[3]), .reset(RESET10_2_out));  // open: Qn, preset
  and and_1 (and_1_out, Left[3], Left[1]);
  and RESET10 (RESET10_out, j_k_ff_8_q, j_k_ff_6_q);
  or or_1 (or_1_out, RESET10_out, RESET);
  and RESET9 (RESET9_out, j_k_ff_8_q, j_k_ff_5_q);
  J_K_Flip_Flop j_k_ff_5 (
    .J(1'b1), .K(1'b1), .clk(SWITCH_MIN), .Q(j_k_ff_5_q), .Qn(j_k_ff_5_qn), .reset(or_1_out));  // open: preset
  D_Flip_Flop #(.trigger("falling")) d_ff_5 (
    .D(j_k_ff_5_q), .clk(SWITCH_MIN), .Q(Right[0]), .reset(or_1_out));  // open: Qn, preset
  J_K_Flip_Flop j_k_ff_6 (
    .J(1'b1), .K(1'b1), .clk(j_k_ff_5_qn), .Q(j_k_ff_6_q), .Qn(j_k_ff_6_qn), .reset(or_1_out));  // open: preset
  D_Flip_Flop #(.trigger("falling")) d_ff_6 (
    .D(j_k_ff_6_q), .clk(SWITCH_MIN), .Q(Right[1]), .reset(or_1_out));  // open: Qn, preset
  J_K_Flip_Flop j_k_ff_7 (
    .J(1'b1), .K(1'b1), .clk(j_k_ff_6_qn), .Q(j_k_ff_7_q), .Qn(j_k_ff_7_qn), .reset(or_1_out));  // open: preset
  J_K_Flip_Flop j_k_ff_8 (.J(1'b1), .K(1'b1), .clk(j_k_ff_7_qn), .Q(j_k_ff_8_q), .reset(or_1_out));  // open: Qn, preset
  D_Flip_Flop #(.trigger("falling")) d_ff_7 (
    .D(j_k_ff_7_q), .clk(SWITCH_MIN), .Q(Right[2]), .reset(or_1_out));  // open: Qn, preset
  D_Flip_Flop #(.trigger("falling")) d_ff_8 (
    .D(j_k_ff_8_q), .clk(SWITCH_MIN), .Q(Right[3]), .reset(or_1_out));  // open: Qn, preset
endmodule

module Step5 (
  input  SPLIT,
  input  is_Start,
  input  Reset,
  input  [3:0] Minutes_1,
  input  [3:0] Minutes_2,
  input  [3:0] Seconds_1,
  input  [3:0] Seconds_2,
  output [3:0] Split_Min_1,
  output [3:0] Split_Min_2,
  output [3:0] Split_Sec_1,
  output [3:0] Split_Sec_2
);

  wire and_1_out;

  and and_1 (and_1_out, SPLIT, is_Start);
  Alpha_register alpha_register_1 (
    .Split(and_1_out), .Reset(Reset), .bits_4_input(Minutes_1), .bits_4_output(Split_Min_1));
  Alpha_register alpha_register_2 (
    .Split(and_1_out), .Reset(Reset), .bits_4_input(Minutes_2), .bits_4_output(Split_Min_2));
  Alpha_register alpha_register_3 (
    .Split(and_1_out), .Reset(Reset), .bits_4_input(Seconds_1), .bits_4_output(Split_Sec_1));
  Alpha_register alpha_register_4 (
    .Split(and_1_out), .Reset(Reset), .bits_4_input(Seconds_2), .bits_4_output(Split_Sec_2));
endmodule

module Step6 (
  input  SPLIT,
  input  is_Start,
  input  Reset,
  input  [3:0] Split_Min_1,
  input  [3:0] Split_Min_2,
  input  [3:0] Split_Sec_1,
  input  [3:0] Split_Sec_2,
  output [3:0] Split_1_Min_1,
  output [3:0] Split_1_Min_2,
  output [3:0] Split_1_Sec_1,
  output [3:0] Split_1_Sec_2,
  output [3:0] Split_2_Min_1,
  output [3:0] Split_2_Min_2,
  output [3:0] Split_2_Sec_1,
  output [3:0] Split_2_Sec_2,
  output [3:0] Split_3_Min_1,
  output [3:0] Split_3_Min_2,
  output [3:0] Split_3_Sec_1,
  output [3:0] Split_3_Sec_2,
  output [3:0] Split_4_Min_1,
  output [3:0] Split_4_Min_2,
  output [3:0] Split_4_Sec_1,
  output [3:0] Split_4_Sec_2,
  output [3:0] Split_5_Min_1,
  output [3:0] Split_5_Min_2,
  output [3:0] Split_5_Sec_1,
  output [3:0] Split_5_Sec_2
);

  wire and_1_out, d_ff_1_q, d_ff_2_q, d_ff_3_q, d_ff_4_q, d_ff_5_q, not_1_out, or_1_out;

  not not_1 (not_1_out, and_1_out);
  and and_1 (and_1_out, SPLIT, is_Start);
  D_Flip_Flop d_ff_1 (.D(not_1_out), .clk(and_1_out), .Q(d_ff_1_q), .reset(or_1_out));  // open: Qn, preset
  Step5 step5_1 (
    .SPLIT(d_ff_1_q), .is_Start(is_Start), .Reset(Reset), .Minutes_1(Split_Min_1), .Minutes_2(Split_Min_2),
    .Seconds_1(Split_Sec_1), .Seconds_2(Split_Sec_2), .Split_Min_1(Split_1_Min_1),
    .Split_Min_2(Split_1_Min_2), .Split_Sec_1(Split_1_Sec_1), .Split_Sec_2(Split_1_Sec_2));
  D_Flip_Flop d_ff_2 (.D(d_ff_1_q), .clk(and_1_out), .Q(d_ff_2_q), .reset(or_1_out));  // open: Qn, preset
  D_Flip_Flop d_ff_3 (.D(d_ff_2_q), .clk(and_1_out), .Q(d_ff_3_q), .reset(or_1_out));  // open: Qn, preset
  Step5 step5_2 (
    .SPLIT(d_ff_2_q), .is_Start(is_Start), .Reset(Reset), .Minutes_1(Split_Min_1), .Minutes_2(Split_Min_2),
    .Seconds_1(Split_Sec_1), .Seconds_2(Split_Sec_2), .Split_Min_1(Split_2_Min_1),
    .Split_Min_2(Split_2_Min_2), .Split_Sec_1(Split_2_Sec_1), .Split_Sec_2(Split_2_Sec_2));
  D_Flip_Flop d_ff_4 (.D(d_ff_3_q), .clk(and_1_out), .Q(d_ff_4_q), .reset(or_1_out));  // open: Qn, preset
  Step5 step5_3 (
    .SPLIT(d_ff_3_q), .is_Start(is_Start), .Reset(Reset), .Minutes_1(Split_Min_1), .Minutes_2(Split_Min_2),
    .Seconds_1(Split_Sec_1), .Seconds_2(Split_Sec_2), .Split_Min_1(Split_3_Min_1),
    .Split_Min_2(Split_3_Min_2), .Split_Sec_1(Split_3_Sec_1), .Split_Sec_2(Split_3_Sec_2));
  D_Flip_Flop d_ff_5 (.D(d_ff_4_q), .clk(and_1_out), .Q(d_ff_5_q), .reset(or_1_out));  // open: Qn, preset
  Step5 step5_4 (
    .SPLIT(d_ff_4_q), .is_Start(is_Start), .Reset(Reset), .Minutes_1(Split_Min_1), .Minutes_2(Split_Min_2),
    .Seconds_1(Split_Sec_1), .Seconds_2(Split_Sec_2), .Split_Min_1(Split_4_Min_1),
    .Split_Min_2(Split_4_Min_2), .Split_Sec_1(Split_4_Sec_1), .Split_Sec_2(Split_4_Sec_2));
  or or_1 (or_1_out, d_ff_5_q, Reset);
  Step5 step5_5 (
    .SPLIT(d_ff_5_q), .is_Start(is_Start), .Reset(Reset), .Minutes_1(Split_Min_1), .Minutes_2(Split_Min_2),
    .Seconds_1(Split_Sec_1), .Seconds_2(Split_Sec_2), .Split_Min_1(Split_5_Min_1),
    .Split_Min_2(Split_5_Min_2), .Split_Sec_1(Split_5_Sec_1), .Split_Sec_2(Split_5_Sec_2));
endmodule

module Alpha_register (
  input  Split,
  input  Reset,
  input  [3:0] bits_4_input,
  output [3:0] bits_4_output
);

  D_Flip_Flop d_ff_1 (.D(bits_4_input[0]), .clk(Split), .Q(bits_4_output[0]), .reset(Reset));  // open: Qn, preset
  D_Flip_Flop d_ff_2 (.D(bits_4_input[1]), .clk(Split), .Q(bits_4_output[1]), .reset(Reset));  // open: Qn, preset
  D_Flip_Flop d_ff_3 (.D(bits_4_input[2]), .clk(Split), .Q(bits_4_output[2]), .reset(Reset));  // open: Qn, preset
  D_Flip_Flop d_ff_4 (.D(bits_4_input[3]), .clk(Split), .Q(bits_4_output[3]), .reset(Reset));  // open: Qn, preset
endmodule
